# Fritzing sketch treadmill version2 (saved by Fritzing 0.9.3b)
breadboards: 1

parts:
  Raspberry_Pi_1 = Raspberry Pi 3 [part_number=RPI-3-V1.2]
  Treadmill_Connector = Header 8 [package=1x08_smd]
  Safety_Switch_Connector = Header 3 [package=screwterminal-3.5mm-3_lock.007s]
  LM1085 = Voltage Regulator - 5V [package="TO220 [THT]"]
  C1 = Tantalum Capacitor [capacitance=10µF package="100 mil [THT, tantalum]"]
  C2 = Electrolytic Capacitor [capacitance=10µF package="100 mil [THT, electrolytic]"]
  X1 = USB Connectors [package=usb-microb]
  R1 = Resistor [tolerance=±5% resistance=1k package=THT]
  R4 = Resistor [tolerance=±5% resistance=100 package=THT]
  C3 = Ceramic Capacitor [capacitance=20nF package="100 mil [THT, multilayer]"]
  R6 = Resistor [tolerance=±5% resistance=100 package=THT]
  R7 = Resistor [tolerance=±5% resistance=100 package=THT]
  C4 = Ceramic Capacitor [capacitance=20nF package="100 mil [THT, multilayer]"]
  IC1 = IC, DIP package, 14 pins [chip_label=IC]

nets:
  N1: Raspberry_Pi_1.3v3, Safety_Switch_Connector.2
  GND: Raspberry_Pi_1.GND, Safety_Switch_Connector.1, LM1085.input_voltage, C1.-, C2.-, X1.GND, C3.0, C4.1, IC1.pin1, IC1.pin4, IC1.pin7
  N2: Raspberry_Pi_1.GIPO17, R4.Pin_1, C3.1
  N3: Raspberry_Pi_1.GIPO27, IC1.pin2
  N4: Raspberry_Pi_1.GIPO22, IC1.pin5
  N5: Raspberry_Pi_1.GIPO24, R6.Pin_1, C4.0
  N6: Raspberry_Pi_1.GIPO23, R7.Pin_1
  N7: Raspberry_Pi_1.GIPO18, R1.Pin_1
  N8: Treadmill_Connector.2, LM1085.output_voltage, C2.+
  N9: Treadmill_Connector.3, R4.Pin_0
  N10: Treadmill_Connector.4, R1.Pin_0
  N11: Treadmill_Connector.5, IC1.pin3
  N12: Treadmill_Connector.6, IC1.pin6
  N13: Treadmill_Connector.7, R7.Pin_0
  N14: Safety_Switch_Connector.3, R6.Pin_0
  N15: LM1085.GND, C1.+, X1.VBUS, IC1.pin14

notes:
  1 - Black, ground
  2 - Red, +9 VDC
  3 - Green, Speed sensor, 0-5 VDC
  4 - Blue, PWM signal to set speed
  5 - Orange, Incline up
  6 - Yellow, Incline down
  7 - Violet, Incline sensor
  8 - Striped black, step counter (MC2100SDI)
  Powering the Pi
  The LM1085 converts the 7-13 VDC from the motor controller to 5 V and can supply 3 A to run the Pi. This is applied via the USB power on the Pi because it has protection circuitry that the GPIO power pins do not.
  The treadmill doesn't seem to be able to deliver enough power to run the Pi though, so I ended up plugging it it. The LM1085 output is still used for the level shifter.
  Black - Ground
  Red - 7-13 VDC
  Green - Speed sensor
  Blue - PWM motor speed driver
  Orange - Incline up
  Yellow - Incline down
  Violet - Incline changing
  Grey - Step counter?
  Raspberry Pi Pins
  11 (GPIO 17) Speed sensor
  12 (GPIO 18) PWM output
  13 (GPIO 27) Incline up
  15 (GPIO 22) Incline down
  16 (GPIO 23) Incline sensor
  18 (GPIO 24) Safety switch
  The Pi doesn't output enough voltage to drive the incline pins, so a level shifter is used to get the orange and yellow signals closer to what the treadmill requires.
  Inputs have LC filters to remove high frequency noise.
