# Fritzing sketch treadmill (saved by Fritzing 0.9.3b)
breadboards: 1

parts:
  Raspberry_Pi_1 = Raspberry Pi 3 [part_number=RPI-3-V1.2]
  R1 = Resistor [tolerance=±5% resistance=150 package=THT]
  R2 = Resistor [tolerance=±5% resistance=150 package=THT]
  JP1 = Header 8 [package=bm08b-srss-tb]
  R5 = Resistor [tolerance=±5% resistance=47k package=THT]
  C1 = Ceramic Capacitor [capacitance=20nF package="100 mil [THT, multilayer]"]
  C2 = Ceramic Capacitor [capacitance=100nF package="100 mil [THT, multilayer]"]
  R6 = Resistor [tolerance=±5% resistance=220 package=THT]

nets:
  GND: Raspberry_Pi_1.GND, R2.Pin_1, JP1.1, C1.0, C2.0
  N1: Raspberry_Pi_1.GIPO17, R5.Pin_1, C1.1
  N2: Raspberry_Pi_1.GIPO21, JP1.5
  N3: Raspberry_Pi_1.GIPO20, JP1.6
  N4: Raspberry_Pi_1.GIPO16, C2.1, R6.Pin_0
  N5: Raspberry_Pi_1.GIPO18, R1.Pin_0
  N6: R1.Pin_1, R2.Pin_0, JP1.4
  N7: JP1.3, R5.Pin_0
  N8: JP1.7, R6.Pin_1

notes:
  1 - Black, ground
  2 - Red, +9 VDC
  3 - Green, Speed sensor, 0-5 VDC
  4 - Blue, PWM signal to set speed
  5 - Orange, Incline up
  6 - Yellow, Incline down
  7 - Violet, Incline sensor
  8 - Striped black, step counter (MC2100SDI)
